// Logisim project P_MEM1.circ as structural Verilog: 2 circuits, main circuit main
module main (
  input  D,
  input  S,
  input  E,
  input  E_2,
  input  R,
  input  D_2,
  input  E_3,
  output Q,
  output Q_2,
  output Q_bar,
  output Q_3,
  output Q_bar_2
);

  wire nand_1_out, nand_2_out, nand_3_out, nand_4_out, nand_9_out, nand_10_out, nand_12_out, not_1_out;

  not not_1 (not_1_out, D_2);
  nand nand_1 (nand_1_out, S, E);
  nand nand_2 (nand_2_out, E, R);
  nand nand_3 (nand_3_out, D_2, E_3);
  nand nand_4 (nand_4_out, E_3, not_1_out);
  nand nand_5 (Q_2, nand_1_out, Q_bar);
  nand nand_6 (Q_bar, Q_2, nand_2_out);
  nand nand_7 (Q_3, nand_3_out, Q_bar_2);
  nand nand_8 (Q_bar_2, Q_3, nand_4_out);
  nand nand_9 (nand_9_out, D, E_2);
  nand nand_10 (nand_10_out, nand_9_out, E_2);
  nand nand_11 (Q, nand_9_out, nand_12_out);
  nand nand_12 (nand_12_out, Q, nand_10_out);

  // Notes on the sheet:
  //   SR
  //   D-FlipFlop 
  //   1-Bit-Memory Cell
endmodule

module P_MEM1 (
  input  D,
  input  E,
  output Q
);

  wire nand_1_out, nand_2_out, nand_4_out;

  nand nand_1 (nand_1_out, D, E);
  nand nand_2 (nand_2_out, nand_1_out, E);
  nand nand_3 (Q, nand_1_out, nand_4_out);
  nand nand_4 (nand_4_out, Q, nand_2_out);

  // Notes on the sheet:
  //   1-Bit-Memory Cell
endmodule
