// Logisim project Processor_8.circ as structural Verilog
module Latches (
  input  D,
  input  S,
  input  E,
  input  E_2,
  input  R,
  input  D_2,
  input  E_3,
  output Q,
  output Q_2,
  output Q_bar,
  output Q_3,
  output Q_bar_2
);

  wire nand_1_out, nand_2_out, nand_3_out, nand_4_out, nand_9_out, nand_10_out, nand_12_out, not_1_out;

  not not_1 (not_1_out, D_2);
  nand nand_1 (nand_1_out, S, E);
  nand nand_2 (nand_2_out, E, R);
  nand nand_3 (nand_3_out, D_2, E_3);
  nand nand_4 (nand_4_out, E_3, not_1_out);
  nand nand_5 (Q_2, nand_1_out, Q_bar);
  nand nand_6 (Q_bar, Q_2, nand_2_out);
  nand nand_7 (Q_3, nand_3_out, Q_bar_2);
  nand nand_8 (Q_bar_2, Q_3, nand_4_out);
  nand nand_9 (nand_9_out, D, E_2);
  nand nand_10 (nand_10_out, nand_9_out, E_2);
  nand nand_11 (Q, nand_9_out, nand_12_out);
  nand nand_12 (nand_12_out, Q, nand_10_out);

  // Notes on the sheet:
  //   SR
  //   D-FlipFlop 
  //   1-Bit-Memory Cell
endmodule

module P_MEM1 (
  input  D,
  input  E,
  output Q
);

  wire nand_1_out, nand_2_out, nand_4_out;

  nand nand_1 (nand_1_out, D, E);
  nand nand_2 (nand_2_out, nand_1_out, E);
  nand nand_3 (Q, nand_1_out, nand_4_out);
  nand nand_4 (nand_4_out, Q, nand_2_out);

  // Notes on the sheet:
  //   1-Bit-Memory Cell
endmodule

module P_MEM8 (
  input  [7:0] in_1,
  input  in_2,
  output [7:0] out_3
);

  P_MEM1 p_mem1_1 (.D(in_1[0]), .E(in_2), .Q(out_3[0]));
  P_MEM1 p_mem1_2 (.D(in_1[1]), .E(in_2), .Q(out_3[1]));
  P_MEM1 p_mem1_3 (.D(in_1[2]), .E(in_2), .Q(out_3[2]));
  P_MEM1 p_mem1_4 (.D(in_1[3]), .E(in_2), .Q(out_3[3]));
  P_MEM1 p_mem1_5 (.D(in_1[4]), .E(in_2), .Q(out_3[4]));
  P_MEM1 p_mem1_6 (.D(in_1[5]), .E(in_2), .Q(out_3[5]));
  P_MEM1 p_mem1_7 (.D(in_1[6]), .E(in_2), .Q(out_3[6]));
  P_MEM1 p_mem1_8 (.D(in_1[7]), .E(in_2), .Q(out_3[7]));
endmodule

module P_ENABLE (
  input  [7:0] in_1,
  input  in_2,
  output [7:0] out_3
);

  and and_1 (out_3[0], in_1[0], in_2);
  and and_2 (out_3[1], in_1[1], in_2);
  and and_3 (out_3[2], in_1[2], in_2);
  and and_4 (out_3[3], in_1[3], in_2);
  and and_5 (out_3[4], in_1[4], in_2);
  and and_6 (out_3[5], in_1[5], in_2);
  and and_7 (out_3[6], in_1[6], in_2);
  and and_8 (out_3[7], in_1[7], in_2);
endmodule

module P_REG_8 (
  input  [7:0] in_1,
  input  E1,
  input  E2,
  output [7:0] out_4
);

  wire [7:0] p_mem8_1_out_3;

  P_MEM8 p_mem8_1 (.in_1(in_1), .out_3(p_mem8_1_out_3), .in_2(E1));
  P_ENABLE p_enable_1 (.in_1(p_mem8_1_out_3), .out_3(out_4), .in_2(E2));
endmodule

module P_REG_8NEW (
  input  [7:0] i,
  input  s,
  input  e,
  output [7:0] REG,
  output [7:0] o
);

  wire [7:0] p_enable_1_out_3;

  P_MEM8 p_mem8_1 (.in_1(i), .out_3(REG), .in_2(s));
  P_ENABLE p_enable_1 (.in_1(REG), .out_3(p_enable_1_out_3), .in_2(e));
  assign o = e ? p_enable_1_out_3 : 8'bz;  // Controlled_Buffer controlled_buffer_1
endmodule

module P_DECODER_4x16 (
  input  [3:0] in_1,
  output out_2,
  output out_3,
  output out_4,
  output out_5,
  output out_6,
  output out_7,
  output out_8,
  output out_9,
  output out_10,
  output out_11,
  output out_12,
  output out_13,
  output out_14,
  output out_15,
  output out_16,
  output out_17
);

  wire not_1_out, not_2_out, not_3_out, not_4_out;

  not not_1 (not_1_out, in_1[0]);
  not not_2 (not_2_out, in_1[1]);
  not not_3 (not_3_out, in_1[2]);
  not not_4 (not_4_out, in_1[3]);
  and and_1 (out_2, not_4_out, not_3_out, not_2_out, not_1_out);
  and and_2 (out_3, not_4_out, not_3_out, not_2_out, in_1[0]);
  and and_3 (out_4, not_4_out, not_3_out, in_1[1], not_1_out);
  and and_4 (out_5, not_4_out, not_3_out, in_1[1], in_1[0]);
  and and_5 (out_6, not_4_out, in_1[2], not_2_out, not_1_out);
  and and_6 (out_7, not_4_out, in_1[2], not_2_out, in_1[0]);
  and and_7 (out_8, not_4_out, in_1[2], in_1[1], not_1_out);
  and and_8 (out_9, not_4_out, in_1[2], in_1[1], in_1[0]);
  and and_9 (out_10, in_1[3], not_3_out, not_2_out, not_1_out);
  and and_10 (out_11, in_1[3], not_3_out, not_2_out, in_1[0]);
  and and_11 (out_12, in_1[3], not_3_out, in_1[1], not_1_out);
  and and_12 (out_13, in_1[3], not_3_out, in_1[1], in_1[0]);
  and and_13 (out_14, in_1[3], in_1[2], not_2_out, not_1_out);
  and and_14 (out_15, in_1[3], in_1[2], not_2_out, in_1[0]);
  and and_15 (out_16, in_1[3], in_1[2], in_1[1], not_1_out);
  and and_16 (out_17, in_1[3], in_1[2], in_1[1], in_1[0]);
endmodule

module P_DECODER_3x8 (
  input  C,
  input  B,
  input  A,
  output [7:0] O
);

  wire not_1_out, not_2_out, not_3_out;

  not not_1 (not_1_out, A);
  not not_2 (not_2_out, B);
  not not_3 (not_3_out, C);
  and and_1 (O[0], not_1_out, not_2_out, not_3_out);
  and and_2 (O[1], not_1_out, not_2_out, C);
  and and_3 (O[2], not_1_out, B, not_3_out);
  and and_4 (O[3], not_1_out, B, C);
  and and_5 (O[4], A, not_2_out, not_3_out);
  and and_6 (O[5], A, not_2_out, C);
  and and_7 (O[6], A, B, not_3_out);
  and and_8 (O[7], A, B, C);
endmodule

module ALU_ADD (
  input  A,
  input  B,
  input  C,
  output S,
  output C_2
);

  wire and_1_out, and_2_out, xor_1_out;

  xor xor_1 (xor_1_out, A, B);
  and and_1 (and_1_out, A, B);
  xor xor_2 (S, xor_1_out, C);
  and and_2 (and_2_out, xor_1_out, C);
  or or_1 (C_2, and_1_out, and_2_out);
endmodule

module ALU_ADDER_8 (
  input  [7:0] in_1,
  input  [7:0] in_2,
  input  in_3,
  output out_4,
  output [7:0] out_5
);

  wire alu_add_2_c_2, alu_add_3_c_2, alu_add_4_c_2, alu_add_5_c_2, alu_add_6_c_2, alu_add_7_c_2,
       alu_add_8_c_2;

  ALU_ADD alu_add_1 (.A(in_1[7]), .B(in_2[7]), .C(alu_add_2_c_2), .S(out_5[7]), .C_2(out_4));
  ALU_ADD alu_add_2 (.A(in_1[6]), .B(in_2[6]), .C(alu_add_3_c_2), .S(out_5[6]), .C_2(alu_add_2_c_2));
  ALU_ADD alu_add_3 (.A(in_1[5]), .B(in_2[5]), .C(alu_add_4_c_2), .S(out_5[5]), .C_2(alu_add_3_c_2));
  ALU_ADD alu_add_4 (.A(in_1[4]), .B(in_2[4]), .C(alu_add_5_c_2), .S(out_5[4]), .C_2(alu_add_4_c_2));
  ALU_ADD alu_add_5 (.A(in_1[3]), .B(in_2[3]), .C(alu_add_6_c_2), .S(out_5[3]), .C_2(alu_add_5_c_2));
  ALU_ADD alu_add_6 (.A(in_1[2]), .B(in_2[2]), .C(alu_add_7_c_2), .S(out_5[2]), .C_2(alu_add_6_c_2));
  ALU_ADD alu_add_7 (.A(in_1[1]), .B(in_2[1]), .C(alu_add_8_c_2), .S(out_5[1]), .C_2(alu_add_7_c_2));
  ALU_ADD alu_add_8 (.A(in_1[0]), .B(in_2[0]), .C(in_3), .S(out_5[0]), .C_2(alu_add_8_c_2));
endmodule

module ALU_SUBRATOR_8 (
  input  [7:0] in_1,
  input  [7:0] in_2,
  output Bout,
  output [7:0] out_4
);

  wire alu_add_1_c_2, alu_add_2_c_2, alu_add_3_c_2, alu_add_4_c_2, alu_add_5_c_2, alu_add_6_c_2,
       alu_add_7_c_2, alu_add_8_c_2, xor_1_out, xor_2_out, xor_3_out, xor_4_out, xor_5_out, xor_6_out,
       xor_7_out, xor_8_out;

  xor xor_1 (xor_1_out, 1'b1, in_2[7]);
  xor xor_2 (xor_2_out, 1'b1, in_2[6]);
  xor xor_3 (xor_3_out, 1'b1, in_2[4]);
  xor xor_4 (xor_4_out, 1'b1, in_2[3]);
  xor xor_5 (xor_5_out, 1'b1, in_2[2]);
  xor xor_6 (xor_6_out, 1'b1, in_2[1]);
  xor xor_7 (xor_7_out, 1'b1, in_2[0]);
  xor xor_8 (xor_8_out, 1'b1, in_2[5]);
  xor xor_9 (Bout, 1'b1, alu_add_1_c_2);
  ALU_ADD alu_add_1 (.A(in_1[7]), .B(xor_1_out), .C(alu_add_2_c_2), .S(out_4[7]), .C_2(alu_add_1_c_2));
  ALU_ADD alu_add_2 (.A(in_1[6]), .B(xor_2_out), .C(alu_add_3_c_2), .S(out_4[6]), .C_2(alu_add_2_c_2));
  ALU_ADD alu_add_3 (.A(in_1[5]), .B(xor_8_out), .C(alu_add_4_c_2), .S(out_4[5]), .C_2(alu_add_3_c_2));
  ALU_ADD alu_add_4 (.A(in_1[4]), .B(xor_3_out), .C(alu_add_5_c_2), .S(out_4[4]), .C_2(alu_add_4_c_2));
  ALU_ADD alu_add_5 (.A(in_1[3]), .B(xor_4_out), .C(alu_add_6_c_2), .S(out_4[3]), .C_2(alu_add_5_c_2));
  ALU_ADD alu_add_6 (.A(in_1[2]), .B(xor_5_out), .C(alu_add_7_c_2), .S(out_4[2]), .C_2(alu_add_6_c_2));
  ALU_ADD alu_add_7 (.A(in_1[1]), .B(xor_6_out), .C(alu_add_8_c_2), .S(out_4[1]), .C_2(alu_add_7_c_2));
  ALU_ADD alu_add_8 (.A(in_1[0]), .B(xor_7_out), .C(1'b1), .S(out_4[0]), .C_2(alu_add_8_c_2));
endmodule

module P_SHL (
  input  Shift_in,
  input  [7:0] in_2,
  output [7:0] out_3,
  output Shift_out
);

  wire [6:0] p_reg_8new_1_o;

  P_REG_BYTE p_reg_byte_1 ();
  P_REG_8NEW p_reg_8new_1 (.i(in_2), .s(1'b1), .e(1'b1), .o({Shift_out, p_reg_8new_1_o}));  // open: REG
  P_REG_8NEW p_reg_8new_2 (.i({p_reg_8new_1_o, Shift_in}), .s(1'b1), .e(1'b1), .o(out_3));  // open: REG
endmodule

module P_SHR (
  input  [7:0] in_1,
  input  Shift_in,
  output Shift_out,
  output [7:0] out_4
);

  wire [7:1] p_reg_8new_1_o;

  P_REG_8NEW p_reg_8new_1 (.i(in_1), .s(1'b1), .e(1'b1), .o({p_reg_8new_1_o, Shift_out}));  // open: REG
  P_REG_8NEW p_reg_8new_2 (.i({Shift_in, p_reg_8new_1_o}), .s(1'b1), .e(1'b1), .o(out_4));  // open: REG
endmodule

module P_NOT (
  input  [7:0] i,
  output [7:0] out_2
);

  not not_1 (out_2[0], i[0]);
  not not_2 (out_2[1], i[1]);
  not not_3 (out_2[2], i[2]);
  not not_4 (out_2[3], i[3]);
  not not_5 (out_2[4], i[4]);
  not not_6 (out_2[5], i[5]);
  not not_7 (out_2[6], i[6]);
  not not_8 (out_2[7], i[7]);
endmodule

module P_AND (
  input  [7:0] a,
  input  [7:0] b,
  output [7:0] o
);

  and and_1 (o[0], a[0], b[0]);
  and and_2 (o[1], a[1], b[1]);
  and and_3 (o[2], a[2], b[2]);
  and and_4 (o[3], a[3], b[3]);
  and and_5 (o[4], a[4], b[4]);
  and and_6 (o[5], a[5], b[5]);
  and and_7 (o[6], a[6], b[6]);
  and and_8 (o[7], a[7], b[7]);
endmodule

module P_OR (
  input  [7:0] a,
  input  [7:0] b,
  output [7:0] _0
);

  or or_1 (_0[0], a[0], b[0]);
  or or_2 (_0[1], a[1], b[1]);
  or or_3 (_0[2], a[2], b[2]);
  or or_4 (_0[3], a[3], b[3]);
  or or_5 (_0[4], a[4], b[4]);
  or or_6 (_0[5], a[5], b[5]);
  or or_7 (_0[6], a[6], b[6]);
  or or_8 (_0[7], a[7], b[7]);
endmodule

module ALU_MAIN (
  input  [7:0] in_1,
  input  [7:0] in_2,
  input  in_3,
  input  in_4,
  input  in_5,
  input  [2:0] in_6,
  output [7:0] out_7,
  output out_8,
  output out_9,
  output [7:0] out_10,
  output out_11
);

  wire decoder_1_out0, decoder_1_out1, decoder_1_out2, decoder_1_out3, decoder_1_out4, decoder_1_out5;
  wire [7:0] alu_adder_8_1_out_5, alu_subrator_8_1_out_4, controlled_buffer_1_out, controlled_buffer_2_out,
       controlled_buffer_5_out, controlled_buffer_6_out, controlled_buffer_7_out, controlled_buffer_8_out,
       p_shl_1_out_3, p_shr_1_out_4;

  Decoder #(.select(3), .enable("false")) decoder_1 (
    .out0(decoder_1_out0), .out1(decoder_1_out1), .out2(decoder_1_out2), .out3(decoder_1_out3),
    .out4(decoder_1_out4), .out5(decoder_1_out5), .sel(in_6));  // open: out6, out7
  assign controlled_buffer_1_out = decoder_1_out3 ? in_2 : 8'bz;  // Controlled_Buffer controlled_buffer_1
  assign controlled_buffer_2_out = decoder_1_out5 ? in_2 : 8'bz;  // Controlled_Buffer controlled_buffer_2
  assign controlled_buffer_1_out = decoder_1_out2 ? in_1 : 8'bz;  // Controlled_Buffer controlled_buffer_3
  assign controlled_buffer_2_out = decoder_1_out4 ? in_1 : 8'bz;  // Controlled_Buffer controlled_buffer_4
  assign controlled_buffer_5_out = decoder_1_out0 ? in_1 : 8'bz;  // Controlled_Buffer controlled_buffer_5
  assign controlled_buffer_6_out = decoder_1_out0 ? in_2 : 8'bz;  // Controlled_Buffer controlled_buffer_6
  assign controlled_buffer_7_out = decoder_1_out1 ? in_1 : 8'bz;  // Controlled_Buffer controlled_buffer_7
  assign controlled_buffer_8_out = decoder_1_out1 ? in_2 : 8'bz;  // Controlled_Buffer controlled_buffer_8
  P_SHL p_shl_1 (.in_2(controlled_buffer_1_out), .out_3(p_shl_1_out_3), .Shift_out(out_9), .Shift_in(in_4));
  P_SHR p_shr_1 (.in_1(controlled_buffer_2_out), .Shift_out(out_11), .out_4(p_shr_1_out_4), .Shift_in(in_5));
  ALU_ADDER_8 alu_adder_8_1 (
    .in_1(controlled_buffer_5_out), .in_2(controlled_buffer_6_out), .out_5(alu_adder_8_1_out_5), .in_3(in_3));  // open: out_4
  ALU_SUBRATOR_8 alu_subrator_8_1 (
    .in_1(controlled_buffer_7_out), .in_2(controlled_buffer_8_out), .out_4(alu_subrator_8_1_out_4),
    .Bout(out_8));
  assign out_7 = decoder_1_out0 ? alu_adder_8_1_out_5 : 8'bz;  // Controlled_Buffer controlled_buffer_9
  assign out_7 = decoder_1_out1 ? alu_subrator_8_1_out_4 : 8'bz;  // Controlled_Buffer controlled_buffer_10
  assign out_10 = decoder_1_out2 ? p_shl_1_out_3 : 8'bz;  // Controlled_Buffer controlled_buffer_11
  Controlled_Buffer #(.width(8)) controlled_buffer_12 (.in(p_shr_1_out_4), .out(out_10));  // open: en
endmodule
